# Fritzing sketch led_runner (saved by Fritzing 0.9.9b)
breadboards: 1

parts:
  LCD1 = LCD screen
  Part1 = Arduino Nano (Rev3.0)
  Part2 = HC-SR501 Body Sensor Module
  BAT1 = BC9VPC [package=bc9vpc]
  U1 = POT [package=pot_mammoth]
  R1 = Resistor [tolerance=±5% resistance=220 package="1206 [SMD]"]
  S1 = Toggle Switch spst [package=THT]
  BAT2 = BC9VPC [package=bc9vpc]

nets:
  GND: LCD1.VSS, LCD1.R/W, LCD1.LED-, Part1.GND, Part2.GND, BAT1.V-, U1.E, BAT2.V-
  VDD: LCD1.VDD, LCD1.LED+, Part1.VIN, Part2.VCC, BAT1.V+, R1.Pin_0, R1.Pin_1, S1.COM
  N1: LCD1.V0, U1.A
  N2: LCD1.RS, Part1.D11/MOSI
  N3: LCD1.E, Part1.D8
  N4: LCD1.DB4, Part1.D6
  N5: LCD1.DB5, Part1.D5
  N6: LCD1.DB6, Part1.D4
  N7: LCD1.DB7, Part1.D3
  N8: Part1.D2, Part2.OUT
  N9: S1.L1, BAT2.V+

custom parts:
  HC-SR501 Body Sensor Module: Pyroelectric Infrared PIR Motion Sensor Detector Module
  Toggle Switch spst: Toggle Switch single pole single throw
