# Fritzing sketch memory_5led (saved by Fritzing 0.9.9b)
breadboards: 1

parts:
  Part1 = Arduino Nano (Rev3.0)
  LED1 = LED - 3mm [color="Yellow (595nm)" current=0.030 package="3 mm [THT]"]
  LED2 = LED - 3mm [color="Red (633nm)" current=0.030 package="3 mm [THT]"]
  LED3 = LED - 3mm [color="Green (560nm)" current=0.030 package="3 mm [THT]"]
  LED4 = LED - 3mm [color="Blue (430nm)" current=0.030 package="3 mm [THT]"]
  R1 = Resistor [tolerance=±5% resistance=220 package="1206 [SMD]"]
  R2 = Resistor [tolerance=±5% resistance=220 package="1206 [SMD]"]
  R3 = Resistor [tolerance=±5% resistance=220 package="1206 [SMD]"]
  R4 = Resistor [tolerance=±5% resistance=220 package="1206 [SMD]"]
  S1 = Pushbutton [package="[THT]"]
  S2 = Pushbutton [package="[THT]"]
  S3 = Pushbutton [package="[THT]"]
  S4 = Pushbutton [package="[THT]"]
  R5 = Resistor [tolerance=±5% resistance=220 package="1206 [SMD]"]
  LED5 = LED - 3mm [color="White (6500K)" current=0.030 package="3 mm [THT]"]
  S5 = Pushbutton [package="[THT]"]
  BAT1 = BC9VPC [package=bc9vpc]
  S6 = Toggle Switch spst [package=THT]

nets:
  N1: Part1.D2, S4.Pin_3, S4.Pin_4
  N2: Part1.D3, R4.Pin_1
  N3: Part1.D5, S3.Pin_3, S3.Pin_4
  N4: Part1.D6, R3.Pin_1
  N5: Part1.D7, S5.Pin_3, S5.Pin_4
  N6: Part1.D8, R5.Pin_1
  N7: Part1.D9, S2.Pin_3, S2.Pin_4
  N8: Part1.D10, R2.Pin_1
  N9: Part1.D11/MOSI, R1.Pin_1
  N10: Part1.D12/MISO, S1.Pin_3, S1.Pin_4
  N11: Part1.VIN, S6.COM
  N12: Part1.GND, BAT1.V-
  N13: LED1.cathode, LED2.cathode, LED3.cathode, LED4.cathode, LED5.cathode
  N14: LED1.anode, R1.Pin_0
  N15: LED2.anode, R2.Pin_0
  N16: LED3.anode, R3.Pin_0
  N17: LED4.anode, R4.Pin_0
  N18: S1.Pin_1, S1.Pin_2, S2.Pin_1, S2.Pin_2, S3.Pin_1, S3.Pin_2, S4.Pin_1, S4.Pin_2, S5.Pin_1, S5.Pin_2
  N19: R5.Pin_0, LED5.anode
  N20: BAT1.V+, S6.L1

custom parts:
  Toggle Switch spst: Toggle Switch single pole single throw
