# Fritzing sketch memory_5led_v2 (saved by Fritzing 0.9.9b)
breadboards: 1

parts:
  Part1 = Arduino Nano (Rev3.0)
  LED1 = LED - 3mm [color="Yellow (595nm)" current=0.030 package="3 mm [THT]"]
  LED2 = LED - 3mm [color="Red (633nm)" current=0.030 package="3 mm [THT]"]
  LED3 = LED - 3mm [color="Green (560nm)" current=0.030 package="3 mm [THT]"]
  LED4 = LED - 3mm [color="Blue (430nm)" current=0.030 package="3 mm [THT]"]
  R1 = Resistor [tolerance=±5% resistance=330 package="1206 [SMD]"]
  R2 = Resistor [tolerance=±5% resistance=330 package="1206 [SMD]"]
  R3 = Resistor [tolerance=±5% resistance=330 package="1206 [SMD]"]
  R4 = Resistor [tolerance=±5% resistance=330 package="1206 [SMD]"]
  S1 = Pushbutton [package="[THT]"]
  S2 = Pushbutton [package="[THT]"]
  S3 = Pushbutton [package="[THT]"]
  S4 = Pushbutton [package="[THT]"]
  R5 = Resistor [tolerance=±5% resistance=330 package="1206 [SMD]"]
  LED5 = LED - 3mm [color="White (6500K)" current=0.030 package="3 mm [THT]"]
  S5 = Pushbutton [package="[THT]"]
  BAT1 = BC9VPC [package=bc9vpc]
  R6 = Resistor [tolerance=±5% resistance=10k package="1206 [SMD]"]
  R7 = Resistor [tolerance=±5% resistance=10k package="1206 [SMD]"]
  R8 = Resistor [tolerance=±5% resistance=10k package="1206 [SMD]"]
  R9 = Resistor [tolerance=±5% resistance=10k package="1206 [SMD]"]
  R10 = Resistor [tolerance=±5% resistance=10k package="1206 [SMD]"]
  U2 = SWITCH_SPDT [package=kps-1290]

nets (from the breadboard view):
  N1: Part1.GND, LED1.cathode, LED2.cathode, LED3.cathode, LED5.cathode, R6.Pin_0, R7.Pin_0, R8.Pin_0, R9.Pin_0, R10.Pin_0, U2.P
  N2: Part1.D2, R5.Pin_1, S5.Pin_3, S5.Pin_4, R6.Pin_1
  N3: Part1.D5, R4.Pin_1, S4.Pin_3, S4.Pin_4, R7.Pin_1
  N4: Part1.D8, R3.Pin_1, S3.Pin_3, S3.Pin_4, R8.Pin_1
  N5: Part1.D10, R2.Pin_1, S2.Pin_3, S2.Pin_4, R9.Pin_1
  N6: Part1.VIN, BAT1.V+
  N7: Part1.D13/SCK, R1.Pin_1, S1.Pin_3, S1.Pin_4, R10.Pin_1
  N8: LED1.anode, R1.Pin_0
  N9: LED2.anode, R2.Pin_0
  N10: LED3.anode, R3.Pin_0
  N11: LED4.anode, R4.Pin_0
  N12: S1.Pin_1, S1.Pin_2, S2.Pin_1, S2.Pin_2, S3.Pin_1, S3.Pin_2, S4.Pin_1, S4.Pin_2, S5.Pin_1, S5.Pin_2
  N13: R5.Pin_0, LED5.anode
  N14: BAT1.V-, U2.O
