# Fritzing sketch snake (saved by Fritzing 0.9.9b)
breadboards: 1

parts:
  Part1 = Arduino Nano (Rev3.0)
  Part3 = Thumb Joystick
  8x8_LED_Modul_mit_MAX1 = 8x8 LED Modul mit MAX7219 [package=THT]
  U1 = POT [package=pot_mammoth]
  BAT1 = BC9VPC [package=bc9vpc]
  U3 = SWITCH_SPDT [package=kps-1290]

nets (from the breadboard view):
  GND: Part1.GND, Part3.GND, 8x8_LED_Modul_mit_MAX1.GND_Eingang, U1.E, U3.P
  N1: Part1.D10, 8x8_LED_Modul_mit_MAX1.CLK_Eingang
  N2: Part1.D11/MOSI, 8x8_LED_Modul_mit_MAX1.CS_Eingang
  N3: Part1.D12/MISO, 8x8_LED_Modul_mit_MAX1.DIN_Eingang
  N4: Part1.VIN, BAT1.V+
  5V: Part1.5V, Part3.VCC, 8x8_LED_Modul_mit_MAX1.VCC_Eingang, U1.S
  N5: Part1.A7, U1.A
  N6: Part1.A3, Part3.HORZ
  N7: Part1.A2, Part3.VERT
  N8: BAT1.V-, U3.O
